# Fritzing sketch echotech (saved by Fritzing 0.9.3b)

parts:
  Bauteil1 = Arduino Uno (Rev3)
  hc-sr1 = hc-sr04
  hc-sr2 = hc-sr04
  U1 = Vibration Motor- ROB-08449 [package=vibe-motor-10mm]
  U2 = Vibration Motor- ROB-08449 [package=vibe-motor-10mm]

nets:
  N1: Bauteil1.D8, hc-sr2.Echo
  N2: Bauteil1.D11_PWM/MOSI, hc-sr1.Trig
  N3: Bauteil1.D12/MISO, hc-sr1.Echo
  N4: Bauteil1.D4, U1.-
  N5: Bauteil1.D5_PWM, U2.-
  N6: Bauteil1.D7, hc-sr2.Trig
  5V: Bauteil1.5V, hc-sr2.VCC
  GND: Bauteil1.GND, hc-sr2.GND
